# Fritzing sketch fritzing_scheme (saved by Fritzing 0.9.4)
breadboards: 1

parts:
  M1 = DOIT Esp32 DevKit v1 (30 pins long, 11 pins width) [part_number=ESP32S-PIN30]
  M2 = ESC
  920KV_Motor1 = DJI 920 KV Motor
  Part1 = Adafruit 1.3in 240x240 IPS TFT [part_number="Adafruit #4313"]
  ENCODER1 = Rotary Encoder with switch (KY-040) [part_number=KY-040]
  U1 = TCRT5000 [package=THT]
  R1 = Resistor [tolerance=±5% resistance=10k package=THT]
  R2 = Resistor [tolerance=±5% resistance=330 package=THT]
  BAT1 = 18650 battery holder [package=battery-18650-kit]
  BAT2 = 18650 battery holder [package=battery-18650-kit]
  BAT3 = 18650 battery holder [package=battery-18650-kit]

nets:
  3V3: M1.3V3, Part1.VIN
  GND: M1.GND, M1.D32, M2.GND, Part1.GND, ENCODER1.GND, ENCODER1.+, U1.Pin_2
  N1: M1.D18, Part1.SCK
  N2: M1.D23, Part1.MISO
  N3: M1.D33, ENCODER1.SW
  N4: M1.D25, ENCODER1.DT
  N5: M1.D26, ENCODER1.CLK
  N6: M1.D27, Part1.TFTDC
  N7: M1.D14, Part1.RESET
  N8: M1.D13, M2.DATA
  VIN: M1.VIN, M2.5V, R1.Pin_0, R2.Pin_0
  N9: M2.U, 920KV_Motor1.u
  N10: M2.V, 920KV_Motor1.v
  N11: M2.W, 920KV_Motor1.w
  N12: U1.Pin_1, R1.Pin_1
  N13: U1.Pin_4, R2.Pin_1
  N14: BAT1.+, BAT2.-
  N15: BAT2.+, BAT3.-

notes:
  CONNECT TO BMS!!

custom parts:
  DOIT Esp32 DevKit v1 (30 pins long, 11 pins width): The DOIT Esp32 DevKit v1 is one of the development board created by DOIT to evaluate the ESP-WROOM-32 module. It is based on the ESP32 microcontroller that boasts Wifi, Bluetooth, Ethernet and Low Power support all in a single chip. (vanepp) made breadboard work, adjusted pin numbering and labels and reduced size of schematic and cleaned up pcb. This chip is 30pins long (2 x15) and 11 pins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
  DJI 920 KV Motor: DJI Brushless Outrunner 2212/920K Motor F330-550
  Adafruit 1.3in 240x240 IPS TFT: We've been looking for a display like this for a long time - it's so small only 1.3" diagonal but has a high density 260 ppi, 240x240 pixel display with full-angle viewing. It looks a lot like our 1.44" 128x128 display, but has 4x as many pixels and looks great at any angle. We've seen displays of this caliber used in smartwatches and small electronic devices but they've always been MIPI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
  Rotary Encoder with switch (KY-040): A Rotary Encoder with switch
  TCRT5000: TCRT5000 optical reflective sensor
  18650 battery holder: 18650 Battery Holder
